# Fritzing sketch schematics (saved by Fritzing 0.9.3b)

parts:
  Part1 = Arduino Nano (Rev3.0)
  M1 = fc-51 [package=THT]
  A1 = HC-SR501 Body Sensor Module
  DFRobot_DFPlayer_Mini1 = DFRobot DFPlayer Mini [part_number=DFR0299]
  SP1 = SPEAKER [package=pcb_mount_speaker]
  BAT1 = Battery Holders [package=battery-aa]
  M3 = DC Motor
  BAT2 = Battery Holders [package=battery-aa]
  M2 = DC Motor
  U1 = 2-Channel 5v Relay Shield [package=relay-2ch5v10a]

nets:
  N1: Part1.D2, U1.IN2
  N2: Part1.D3, U1.IN1
  N3: Part1.D10, DFRobot_DFPlayer_Mini1.TX
  N4: Part1.D11/MOSI, DFRobot_DFPlayer_Mini1.RX
  N5: Part1.A1, A1.OUT
  N6: Part1.A0, M1.pin1
  N7: DFRobot_DFPlayer_Mini1.SPK_1, SP1.-
  N8: DFRobot_DFPlayer_Mini1.SPK_2, SP1.+
  N9: BAT1.-, M3.pin_1
  N10: BAT1.+, U1.K2-In
  N11: M3.pin_2, U1.K2-On
  N12: BAT2.-, M2.pin_1
  N13: BAT2.+, U1.K1-In
  N14: M2.pin_2, U1.K1-On

notes:
  soap pump
  coocoo
  5v is close to the red component

custom parts:
  HC-SR501 Body Sensor Module: Pyroelectric Infrared PIR Motion Sensor Detector Module
  2-Channel 5v Relay Shield: 2 Channel 5v Relay Shield w. 2x SPD-06VDC-SD-C
